// Logisim project Carry_Lookahead_Adder.circ as structural Verilog: 4 circuits, main circuit main
module main (
  input  [15:0] in_1,
  input  [15:0] in_2,
  input  in_3,
  output out_4,
  output out_5,
  output out_6,
  output [15:0] out_7
);

  cla16 cla16_1 (.Bit_15to0_A(in_1), .Bit_15to0_B(in_2), .Cin(in_3), .GG(out_4), .PG(out_5), .C(out_6), .S(out_7));
endmodule

module pfa (
  input  A,
  input  B,
  input  C,
  output P,
  output S,
  output G
);

  xor xor_1 (P, A, B);
  and and_1 (G, A, B);
  xor xor_2 (S, P, C);
endmodule

module cla4 (
  input  [3:0] Bit_3to0_A,
  input  [3:0] Bit_3to0_B,
  input  Cin,
  output GG,
  output PG,
  output C,
  output [3:0] S
);

  wire and_1_out, and_2_out, and_3_out, and_4_out, and_5_out, and_6_out, and_7_out, and_8_out, and_9_out,
       and_10_out, and_11_out, and_12_out, and_13_out, Bit_0_g, Bit_0_p, Bit_1_g, Bit_1_p, Bit_2_g, Bit_2_p,
       Bit_3_g, Bit_3_p, or_1_out, or_2_out, or_3_out;

  pfa Bit_3 (.A(Bit_3to0_A[3]), .B(Bit_3to0_B[3]), .C(or_3_out), .P(Bit_3_p), .S(S[3]), .G(Bit_3_g));
  pfa Bit_2 (.A(Bit_3to0_A[2]), .B(Bit_3to0_B[2]), .C(or_2_out), .P(Bit_2_p), .S(S[2]), .G(Bit_2_g));
  pfa Bit_1 (.A(Bit_3to0_A[1]), .B(Bit_3to0_B[1]), .C(or_1_out), .P(Bit_1_p), .S(S[1]), .G(Bit_1_g));
  pfa Bit_0 (.A(Bit_3to0_A[0]), .B(Bit_3to0_B[0]), .C(Cin), .P(Bit_0_p), .S(S[0]), .G(Bit_0_g));
  and and_1 (and_1_out, Bit_1_p, Bit_0_p, Cin);
  and and_2 (and_2_out, Bit_1_p, Bit_0_g);
  and and_3 (and_3_out, Bit_0_p, Cin);
  and and_4 (and_4_out, Bit_2_p, Bit_1_p, Bit_0_p, Cin);
  and and_5 (and_5_out, Bit_2_p, Bit_1_p, Bit_0_g);
  and and_6 (and_6_out, Bit_2_p, Bit_1_g);
  or or_1 (or_1_out, and_3_out, Bit_0_g);
  and and_7 (and_7_out, Bit_3_p, Bit_2_p, Bit_1_p, Bit_0_g);
  and and_8 (and_8_out, Bit_3_p, Bit_2_p, Bit_1_g);
  and and_9 (and_9_out, Bit_3_p, Bit_2_g);
  and and_10 (and_10_out, Bit_3_p, Bit_2_p, Bit_1_p, Bit_0_p, Cin);
  and and_11 (and_11_out, Bit_3_p, Bit_2_p, Bit_1_p, Bit_0_g);
  and and_12 (and_12_out, Bit_3_p, Bit_2_p, Bit_1_g);
  and and_13 (and_13_out, Bit_3_p, Bit_2_g);
  or or_2 (or_2_out, Bit_1_g, and_1_out, and_2_out);
  or or_3 (or_3_out, Bit_2_g, and_4_out, and_5_out, and_6_out);
  or or_4 (GG, Bit_3_g, and_7_out, and_8_out, and_9_out);
  and and_14 (PG, Bit_3_p, Bit_2_p, Bit_1_p, Bit_0_p);
  or or_5 (C, Bit_3_g, and_10_out, and_11_out, and_12_out, and_13_out);
endmodule

module cla16 (
  input  [15:0] Bit_15to0_A,
  input  [15:0] Bit_15to0_B,
  input  Cin,
  output GG,
  output PG,
  output C,
  output [15:0] S
);

  wire and_1_out, and_2_out, and_3_out, and_4_out, and_5_out, and_6_out, and_8_out, and_9_out, and_10_out,
       and_11_out, and_12_out, and_13_out, and_14_out, cla4_1_gg, cla4_1_pg, cla4_2_gg, cla4_2_pg, cla4_3_gg,
       cla4_3_pg, cla4_4_gg, cla4_4_pg, or_1_out, or_2_out, or_4_out;

  cla4 cla4_1 (
    .Bit_3to0_A(Bit_15to0_A[15:12]), .Bit_3to0_B(Bit_15to0_B[15:12]), .Cin(or_4_out), .GG(cla4_1_gg),
    .PG(cla4_1_pg), .S(S[15:12]));  // open: C
  cla4 cla4_2 (
    .Bit_3to0_A(Bit_15to0_A[11:8]), .Bit_3to0_B(Bit_15to0_B[11:8]), .Cin(or_2_out), .GG(cla4_2_gg),
    .PG(cla4_2_pg), .S(S[11:8]));  // open: C
  cla4 cla4_3 (
    .Bit_3to0_A(Bit_15to0_A[7:4]), .Bit_3to0_B(Bit_15to0_B[7:4]), .Cin(or_1_out), .GG(cla4_3_gg),
    .PG(cla4_3_pg), .S(S[7:4]));  // open: C
  cla4 cla4_4 (
    .Bit_3to0_A(Bit_15to0_A[3:0]), .Bit_3to0_B(Bit_15to0_B[3:0]), .Cin(Cin), .GG(cla4_4_gg), .PG(cla4_4_pg),
    .S(S[3:0]));  // open: C
  and and_1 (and_1_out, cla4_4_pg, Cin);
  and and_2 (and_2_out, cla4_3_pg, cla4_4_pg, Cin);
  and and_3 (and_3_out, cla4_3_pg, cla4_4_pg);
  or or_1 (or_1_out, cla4_4_gg, and_1_out);
  and and_4 (and_4_out, cla4_1_pg, cla4_2_pg, cla4_3_pg, cla4_4_gg);
  and and_5 (and_5_out, cla4_1_pg, cla4_2_pg, cla4_3_gg);
  and and_6 (and_6_out, cla4_1_pg, cla4_2_gg);
  and and_7 (PG, cla4_1_pg, cla4_2_pg, cla4_3_pg, cla4_4_pg);
  and and_8 (and_8_out, cla4_1_pg, cla4_2_pg, cla4_3_pg, cla4_4_pg, Cin);
  and and_9 (and_9_out, cla4_1_pg, cla4_2_pg, cla4_3_pg, cla4_4_gg);
  and and_10 (and_10_out, cla4_1_pg, cla4_2_pg, cla4_3_gg);
  and and_11 (and_11_out, cla4_1_pg, cla4_2_gg);
  and and_12 (and_12_out, cla4_2_pg, cla4_3_pg, cla4_4_pg, Cin);
  and and_13 (and_13_out, cla4_2_pg, cla4_3_pg, cla4_4_gg);
  and and_14 (and_14_out, cla4_2_pg, cla4_3_gg);
  or or_2 (or_2_out, cla4_3_gg, and_2_out, and_3_out);
  or or_3 (GG, cla4_1_gg, and_4_out, and_5_out, and_6_out);
  or or_4 (or_4_out, cla4_2_gg, and_12_out, and_13_out, and_14_out);
  or or_5 (C, cla4_1_gg, and_8_out, and_9_out, and_10_out, and_11_out);
endmodule
