// Logisim project Carry_Select_Adder_16bit.circ as structural Verilog: 4 circuits, main circuit main
module main (
  input  [15:0] in_1,
  input  [15:0] in_2,
  output out_3,
  output [15:0] out_4
);

  csa16 csa16_1 (.CSA16_A(in_1), .CSA16_B(in_2), .C(out_3), .CSA16_out(out_4));
endmodule

module fa (
  input  A,
  input  B,
  input  Cin,
  output S,
  output C
);

  wire and_1_out, and_2_out, xor_1_out;

  xor xor_1 (xor_1_out, A, B);
  and and_1 (and_1_out, A, B);
  xor xor_2 (S, xor_1_out, Cin);
  and and_2 (and_2_out, xor_1_out, Cin);
  or or_1 (C, and_2_out, and_1_out);
endmodule

module fa4 (
  input  Bit3_A,
  input  Bit3_B,
  input  Bit2_A,
  input  Bit2_B,
  input  Bit1_A,
  input  Bit1_B,
  input  Bit0_A,
  input  Bit0_B,
  input  Bit0_Cin,
  output Bit3_S,
  output Bit3_C,
  output Bit2_S,
  output Bit1_S,
  output Bit0_S
);

  wire Bit0_c, bit1_c, bit2_c;

  fa bit3 (.A(Bit3_A), .B(Bit3_B), .Cin(bit2_c), .S(Bit3_S), .C(Bit3_C));
  fa bit2 (.A(Bit2_A), .B(Bit2_B), .Cin(bit1_c), .S(Bit2_S), .C(bit2_c));
  fa bit1 (.A(Bit1_A), .B(Bit1_B), .Cin(Bit0_c), .S(Bit1_S), .C(bit1_c));
  fa Bit0 (.A(Bit0_A), .B(Bit0_B), .Cin(Bit0_Cin), .S(Bit0_S), .C(Bit0_c));
endmodule

module csa16 (
  input  [15:0] CSA16_A,
  input  [15:0] CSA16_B,
  output C,
  output [15:0] CSA16_out
);

  wire Bit_3to0_bit3_c, Bit_7to4_0_bit0_s, Bit_7to4_0_bit1_s, Bit_7to4_0_bit2_s, Bit_7to4_0_bit3_c,
       Bit_7to4_0_bit3_s, Bit_7to4_1_bit0_s, Bit_7to4_1_bit1_s, Bit_7to4_1_bit2_s, Bit_7to4_1_bit3_c,
       Bit_7to4_1_bit3_s, Bit_11to8_0_bit0_s, Bit_11to8_0_bit1_s, Bit_11to8_0_bit2_s, Bit_11to8_0_bit3_c,
       Bit_11to8_0_bit3_s, Bit_11to8_1_bit0_s, Bit_11to8_1_bit1_s, Bit_11to8_1_bit2_s, Bit_11to8_1_bit3_c,
       Bit_11to8_1_bit3_s, Bit_15to12_0_bit0_s, Bit_15to12_0_bit1_s, Bit_15to12_0_bit2_s,
       Bit_15to12_0_bit3_c, Bit_15to12_0_bit3_s, Bit_15to12_1_bit0_s, Bit_15to12_1_bit1_s,
       Bit_15to12_1_bit2_s, Bit_15to12_1_bit3_c, Bit_15to12_1_bit3_s, multiplexer_1_out, multiplexer_6_out;

  fa4 Bit_3to0 (
    .Bit3_A(CSA16_A[3]), .Bit3_B(CSA16_B[3]), .Bit2_A(CSA16_A[2]), .Bit2_B(CSA16_B[2]), .Bit1_A(CSA16_A[1]),
    .Bit1_B(CSA16_B[1]), .Bit0_A(CSA16_A[0]), .Bit0_B(CSA16_B[0]), .Bit0_Cin(1'b0), .Bit3_S(CSA16_out[3]),
    .Bit3_C(Bit_3to0_bit3_c), .Bit2_S(CSA16_out[2]), .Bit1_S(CSA16_out[1]), .Bit0_S(CSA16_out[0]));
  fa4 Bit_7to4_1 (
    .Bit3_A(CSA16_A[7]), .Bit3_B(CSA16_B[7]), .Bit2_A(CSA16_A[6]), .Bit2_B(CSA16_B[6]), .Bit1_A(CSA16_A[5]),
    .Bit1_B(CSA16_B[5]), .Bit0_A(CSA16_A[4]), .Bit0_B(CSA16_B[4]), .Bit0_Cin(1'b1),
    .Bit3_S(Bit_7to4_1_bit3_s), .Bit3_C(Bit_7to4_1_bit3_c), .Bit2_S(Bit_7to4_1_bit2_s),
    .Bit1_S(Bit_7to4_1_bit1_s), .Bit0_S(Bit_7to4_1_bit0_s));
  fa4 Bit_7to4_0 (
    .Bit3_A(CSA16_A[7]), .Bit3_B(CSA16_B[7]), .Bit2_A(CSA16_A[6]), .Bit2_B(CSA16_B[6]), .Bit1_A(CSA16_A[5]),
    .Bit1_B(CSA16_B[5]), .Bit0_A(CSA16_A[4]), .Bit0_B(CSA16_B[4]), .Bit0_Cin(1'b0),
    .Bit3_S(Bit_7to4_0_bit3_s), .Bit3_C(Bit_7to4_0_bit3_c), .Bit2_S(Bit_7to4_0_bit2_s),
    .Bit1_S(Bit_7to4_0_bit1_s), .Bit0_S(Bit_7to4_0_bit0_s));
  Multiplexer multiplexer_1 (
    .in0(Bit_7to4_0_bit3_c), .in1(Bit_7to4_1_bit3_c), .out(multiplexer_1_out), .sel(Bit_3to0_bit3_c));
  fa4 Bit_11to8_1 (
    .Bit3_A(CSA16_A[11]), .Bit3_B(CSA16_B[11]), .Bit2_A(CSA16_A[10]), .Bit2_B(CSA16_B[10]),
    .Bit1_A(CSA16_A[9]), .Bit1_B(CSA16_B[9]), .Bit0_A(CSA16_A[8]), .Bit0_B(CSA16_B[8]), .Bit0_Cin(1'b1),
    .Bit3_S(Bit_11to8_1_bit3_s), .Bit3_C(Bit_11to8_1_bit3_c), .Bit2_S(Bit_11to8_1_bit2_s),
    .Bit1_S(Bit_11to8_1_bit1_s), .Bit0_S(Bit_11to8_1_bit0_s));
  fa4 Bit_11to8_0 (
    .Bit3_A(CSA16_A[11]), .Bit3_B(CSA16_B[11]), .Bit2_A(CSA16_A[10]), .Bit2_B(CSA16_B[10]),
    .Bit1_A(CSA16_A[9]), .Bit1_B(CSA16_B[9]), .Bit0_A(CSA16_A[8]), .Bit0_B(CSA16_B[8]), .Bit0_Cin(1'b0),
    .Bit3_S(Bit_11to8_0_bit3_s), .Bit3_C(Bit_11to8_0_bit3_c), .Bit2_S(Bit_11to8_0_bit2_s),
    .Bit1_S(Bit_11to8_0_bit1_s), .Bit0_S(Bit_11to8_0_bit0_s));
  Multiplexer multiplexer_2 (
    .in0(Bit_7to4_0_bit3_s), .in1(Bit_7to4_1_bit3_s), .out(CSA16_out[7]), .sel(Bit_3to0_bit3_c));
  Multiplexer multiplexer_3 (
    .in0(Bit_7to4_0_bit2_s), .in1(Bit_7to4_1_bit2_s), .out(CSA16_out[6]), .sel(Bit_3to0_bit3_c));
  Multiplexer multiplexer_4 (
    .in0(Bit_7to4_0_bit1_s), .in1(Bit_7to4_1_bit1_s), .out(CSA16_out[5]), .sel(Bit_3to0_bit3_c));
  Multiplexer multiplexer_5 (
    .in0(Bit_7to4_0_bit0_s), .in1(Bit_7to4_1_bit0_s), .out(CSA16_out[4]), .sel(Bit_3to0_bit3_c));
  Multiplexer multiplexer_6 (
    .in0(Bit_11to8_0_bit3_c), .in1(Bit_11to8_1_bit3_c), .out(multiplexer_6_out), .sel(multiplexer_1_out));
  fa4 Bit_15to12_1 (
    .Bit3_A(CSA16_A[15]), .Bit3_B(CSA16_B[15]), .Bit2_A(CSA16_A[14]), .Bit2_B(CSA16_B[14]),
    .Bit1_A(CSA16_A[13]), .Bit1_B(CSA16_B[13]), .Bit0_A(CSA16_A[12]), .Bit0_B(CSA16_B[12]), .Bit0_Cin(1'b1),
    .Bit3_S(Bit_15to12_1_bit3_s), .Bit3_C(Bit_15to12_1_bit3_c), .Bit2_S(Bit_15to12_1_bit2_s),
    .Bit1_S(Bit_15to12_1_bit1_s), .Bit0_S(Bit_15to12_1_bit0_s));
  fa4 Bit_15to12_0 (
    .Bit3_A(CSA16_A[15]), .Bit3_B(CSA16_B[15]), .Bit2_A(CSA16_A[14]), .Bit2_B(CSA16_B[14]),
    .Bit1_A(CSA16_A[13]), .Bit1_B(CSA16_B[13]), .Bit0_A(CSA16_A[12]), .Bit0_B(CSA16_B[12]), .Bit0_Cin(1'b0),
    .Bit3_S(Bit_15to12_0_bit3_s), .Bit3_C(Bit_15to12_0_bit3_c), .Bit2_S(Bit_15to12_0_bit2_s),
    .Bit1_S(Bit_15to12_0_bit1_s), .Bit0_S(Bit_15to12_0_bit0_s));
  Multiplexer multiplexer_7 (
    .in0(Bit_11to8_0_bit3_s), .in1(Bit_11to8_1_bit3_s), .out(CSA16_out[11]), .sel(multiplexer_1_out));
  Multiplexer multiplexer_8 (
    .in0(Bit_11to8_0_bit2_s), .in1(Bit_11to8_1_bit2_s), .out(CSA16_out[10]), .sel(multiplexer_1_out));
  Multiplexer multiplexer_9 (
    .in0(Bit_11to8_0_bit1_s), .in1(Bit_11to8_1_bit1_s), .out(CSA16_out[9]), .sel(multiplexer_1_out));
  Multiplexer multiplexer_10 (
    .in0(Bit_11to8_0_bit0_s), .in1(Bit_11to8_1_bit0_s), .out(CSA16_out[8]), .sel(multiplexer_1_out));
  Multiplexer multiplexer_11 (.in0(Bit_15to12_0_bit3_c), .in1(Bit_15to12_1_bit3_c), .out(C), .sel(multiplexer_6_out));
  Multiplexer multiplexer_12 (
    .in0(Bit_15to12_0_bit3_s), .in1(Bit_15to12_1_bit3_s), .out(CSA16_out[15]), .sel(multiplexer_6_out));
  Multiplexer multiplexer_13 (
    .in0(Bit_15to12_0_bit2_s), .in1(Bit_15to12_1_bit2_s), .out(CSA16_out[14]), .sel(multiplexer_6_out));
  Multiplexer multiplexer_14 (
    .in0(Bit_15to12_0_bit1_s), .in1(Bit_15to12_1_bit1_s), .out(CSA16_out[13]), .sel(multiplexer_6_out));
  Multiplexer multiplexer_15 (
    .in0(Bit_15to12_0_bit0_s), .in1(Bit_15to12_1_bit0_s), .out(CSA16_out[12]), .sel(multiplexer_6_out));
endmodule
